// Logisim project ALU.circ as structural Verilog: 19 circuits, main circuit main
module main (
  input  [31:0] A,
  input  [31:0] B,
  input  Carry,
  input  [4:0] Shift,
  input  [3:0] codop
);

  wire [3:0] ALU_flags;
  wire [31:0] ALU_output;

  ALU ALU (.A(A), .B(B), .Carry(Carry), .Shift(Shift), .Codop(codop), .\output (ALU_output), .Flags(ALU_flags));
  // Probe on ALU_output
  // Probe on ALU_flags
endmodule

module ALU (
  input  [31:0] A,
  input  [31:0] B,
  input  Carry,
  input  [4:0] Shift,
  input  [3:0] Codop,
  output [31:0] \output ,
  output [3:0] Flags
);

  wire bitselector_1_out, bitselector_2_out, bitselector_3_out, Carry_0101, Carry_0110, Carry_1001,
       Carry_1010, Carry_1011, subtractor_1_out, V_prime;
  wire [31:0] A_and_B_2_out, A_and_B_out, A_or_B_out, A_xor_B_out, adder_1_out, adder_2_out, and_1_out,
       multiplier_1_out, not_1_out, shifter_1_out, shifter_2_out, shifter_3_out, shifter_4_out,
       subtractor_2_out, subtractor_3_out, subtractor_4_out;

  BitSelector #(.width(32)) bitselector_1 (.in(A), .out(bitselector_1_out), .sel({5{1'b1}}));
  BitSelector #(.width(32)) bitselector_2 (.in(B), .out(bitselector_2_out), .sel({5{1'b1}}));
  BitSelector #(.width(32)) bitselector_3 (.in(\output ), .out(bitselector_3_out), .sel({5{1'b1}}));
  assign not_1_out = ~B;  // NOT_Gate not_1, 32 bits wide
  decodeurOVF OVF (.a(bitselector_1_out), .b(bitselector_2_out), .s(bitselector_3_out), .v(V_prime));
  assign A_and_B_out = A & B;  // AND_Gate A_and_B, 32 bits wide
  assign A_xor_B_out = A ^ B;  // XOR_Gate A_xor_B, 32 bits wide
  Shifter #(.width(32)) shifter_1 (.in(B), .\dist (Shift), .out(shifter_1_out));
  Shifter #(.width(32), .shift("lr")) shifter_2 (.in(B), .\dist (Shift), .out(shifter_2_out));
  Shifter #(.width(32), .shift("ar")) shifter_3 (.in(B), .\dist (Shift), .out(shifter_3_out));
  Adder #(.width(32)) adder_1 (.a(B), .b(A), .out(adder_1_out), .cin(Carry), .cout(Carry_0101));
  Subtractor #(.width(1)) subtractor_1 (.a(Carry), .b(1'b1), .out(subtractor_1_out));  // open: bin, bout
  Subtractor #(.width(32)) subtractor_2 (
    .a(A), .b(B), .out(subtractor_2_out), .bin(subtractor_1_out), .bout(Carry_0110));
  Shifter #(.width(32), .shift("rr")) shifter_4 (.in(B), .\dist (Shift), .out(shifter_4_out));
  assign A_and_B_2_out = B & A;  // AND_Gate A_and_B_2, 32 bits wide
  Subtractor #(.width(32)) subtractor_3 (
    .a({32{1'b0}}), .b(A), .out(subtractor_3_out), .bout(Carry_1001));  // open: bin
  Subtractor #(.width(32)) subtractor_4 (.a(A), .b(B), .out(subtractor_4_out), .bout(Carry_1010));  // open: bin
  Adder #(.width(32)) adder_2 (.a(A), .b(B), .out(adder_2_out), .cout(Carry_1011));  // open: cin
  assign A_or_B_out = A | B;  // OR_Gate A_or_B, 32 bits wide
  Multiplier #(.width(32)) multiplier_1 (.a(A), .b(B), .out(multiplier_1_out));  // open: cin, cout
  assign and_1_out = not_1_out & A;  // AND_Gate and_1, 32 bits wide
  Multiplexer #(.select(4)) multiplexer_1 (
    .in0(1'b0), .in1(1'b0), .in2(1'b0), .in3(1'b0), .in4(1'b0), .in5(V_prime), .in6(V_prime), .in7(1'b0),
    .in8(1'b0), .in9(1'b0), .in10(V_prime), .in11(V_prime), .in12(1'b0), .in13(1'b0), .in14(1'b0),
    .in15(1'b0), .out(Flags[0]), .sel(Codop));  // open: en
  BitSelector #(.width(32)) bitselector_4 (.in(\output ), .out(Flags[3]), .sel({5{1'b1}}));
  Multiplexer #(.select(4), .width(32)) multiplexer_2 (
    .in0(A_and_B_out), .in1(A_xor_B_out), .in2(shifter_1_out), .in3(shifter_2_out), .in4(shifter_3_out),
    .in5(adder_1_out), .in6(subtractor_2_out), .in7(shifter_4_out), .in8(A_and_B_2_out),
    .in9(subtractor_3_out), .in10(subtractor_4_out), .in11(adder_2_out), .in12(A_or_B_out),
    .in13(multiplier_1_out), .in14(and_1_out), .in15(not_1_out), .out(\output ), .sel(Codop));  // open: en
  // Probe on \output 
  Comparator #(.width(32)) comparator_1 (.a(\output ), .b({32{1'b0}}), .eq(Flags[2]));  // open: gt, lt
  Multiplexer #(.select(4)) multiplexer_3 (
    .in0(1'b0), .in1(1'b0), .in2(1'b0), .in3(1'b0), .in4(1'b0), .in5(Carry_0101), .in6(Carry_0110),
    .in7(1'b0), .in8(1'b0), .in9(Carry_1001), .in10(Carry_1010), .in11(Carry_1011), .in12(1'b0), .in13(1'b0),
    .in14(1'b0), .in15(1'b0), .out(Flags[1]), .sel(Codop));  // open: en

  // Other names for the same wires on the sheet: V = Flags[0]; C = Flags[1]; Z = Flags[2]; N = Flags[3]

  // Notes on the sheet:
  //   Overflow 1
  //   Overflow 2
  //   Output négatif
  //   Flags Splitter
  //   Output Nul
endmodule

module decodeurOVF (
  input  a,
  input  b,
  input  s,
  output v
);

  wire and_1_out, and_2_out, not_1_out, not_2_out, not_3_out;

  not not_1 (not_1_out, a);
  not not_2 (not_2_out, b);
  not not_3 (not_3_out, s);
  and and_1 (and_1_out, not_1_out, not_2_out, s);
  and and_2 (and_2_out, a, b, not_3_out);
  or or_1 (v, and_1_out, and_2_out);
endmodule

module Test_1_A_AND_B (
);

  wire [3:0] ALU_flags;
  wire [31:0] ALU_output;

  // Probe on 32'hffff0f00
  // Probe on 32'hf0ffff
  // Probe on 32'hffff0f00
  // Probe on 32'hf0ffff
  ALU ALU (
    .A(32'hf0ffff), .B(32'hffff0f00), .Codop(4'b0000), .\output (ALU_output), .Flags(ALU_flags));  // open: Carry, Shift
  // Probe on ALU_output
  // Probe on ALU_output
  // Probe on ALU_flags

  // Notes on the sheet:
  //   Input A (héxa)
  //   Input B (héxa)
  //   codop
endmodule

module Test_2_A_XOR_B (
);

  wire [3:0] ALU_flags;
  wire [31:0] ALU_output;

  // Probe on 32'hffff0f00
  // Probe on 32'hffff
  // Probe on 32'hffff0f00
  // Probe on 32'hffff
  ALU ALU (
    .A(32'hffff), .B(32'hffff0f00), .Codop(4'b0001), .\output (ALU_output), .Flags(ALU_flags));  // open: Carry, Shift
  // Probe on ALU_output
  // Probe on ALU_output
  // Probe on ALU_flags

  // Notes on the sheet:
  //   Input A (héxa)
  //   Input B (héxa)
  //   codop
endmodule

module Test_3_Shift_B (
);

  wire [3:0] ALU_flags;
  wire [31:0] ALU_output;

  // Probe on 32'hc0000ff
  // Probe on 32'hc0000ff
  ALU ALU (
    .B(32'hc0000ff), .Shift(5'b00100), .Codop(4'b0010), .\output (ALU_output), .Flags(ALU_flags));  // open: A, Carry
  // Probe on ALU_output
  // Probe on ALU_output
  // Probe on ALU_flags

  // Notes on the sheet:
  //   Input B (héxa)
  //   codop
  //   shift
endmodule

module Test_4_Right_Shift_B (
);

  wire [3:0] ALU_flags;
  wire [31:0] ALU_output;

  // Probe on 32'hff0000c0
  // Probe on 32'hff0000c0
  ALU ALU (
    .B(32'hff0000c0), .Shift(5'b00100), .Codop(4'b0011), .\output (ALU_output), .Flags(ALU_flags));  // open: A, Carry
  // Probe on ALU_output
  // Probe on ALU_output
  // Probe on ALU_flags

  // Notes on the sheet:
  //   Input B (héxa)
  //   codop
  //   shift
endmodule

module Test_5_Arith_Shift_B (
);

  wire [3:0] ALU_flags;
  wire [31:0] ALU_output;

  // Probe on 32'hff00f0c0
  // Probe on 32'hff00f0c0
  ALU ALU (
    .B(32'hff00f0c0), .Shift(5'b00011), .Codop(4'b0100), .\output (ALU_output), .Flags(ALU_flags));  // open: A, Carry
  // Probe on ALU_output
  // Probe on ALU_output
  // Probe on ALU_flags

  // Notes on the sheet:
  //   Input B (héxa)
  //   codop
  //   shift
endmodule

module Test_6_A_B_Carry (
);

  wire [3:0] ALU_flags;
  wire [31:0] ALU_output;

  // Probe on 32'hd
  // Probe on 32'hc
  // Probe on 32'hd
  // Probe on 32'hc
  ALU ALU (
    .A(32'hc), .B(32'hd), .Carry(1'b1), .Codop(4'b0101), .\output (ALU_output), .Flags(ALU_flags));  // open: Shift
  // Probe on ALU_output
  // Probe on ALU_output
  // Probe on ALU_flags

  // Notes on the sheet:
  //   Input A (héxa)
  //   Input B (héxa)
  //   codop
  //   carry
endmodule

module Test_7_A_B__Carry_1 (
);

  wire [3:0] ALU_flags;
  wire [31:0] ALU_output;

  // Probe on 32'hfff
  // Probe on 32'hfff
  // Probe on 32'hfff
  // Probe on 32'hfff
  ALU ALU (
    .A(32'hfff), .B(32'hfff), .Carry(1'b0), .Codop(4'b0110), .\output (ALU_output), .Flags(ALU_flags));  // open: Shift
  // Probe on ALU_output
  // Probe on ALU_output
  // Probe on ALU_flags

  // Notes on the sheet:
  //   Input A (héxa)
  //   Input B (héxa)
  //   codop
  //   carry
endmodule

module Test_8_Rot_Shift_B (
);

  wire [3:0] ALU_flags;
  wire [31:0] ALU_output;

  // Probe on 32'hff
  // Probe on 32'hff
  ALU ALU (.B(32'hff), .Shift(5'b00011), .Codop(4'b0111), .\output (ALU_output), .Flags(ALU_flags));  // open: A, Carry
  // Probe on ALU_output
  // Probe on ALU_output
  // Probe on ALU_flags

  // Notes on the sheet:
  //   Input B (héxa)
  //   codop
  //   shift
endmodule

module Test_9_A_AND_B__TST (
);

  wire [3:0] ALU_flags;
  wire [31:0] ALU_output;

  // Probe on 32'hffff0f00
  // Probe on 32'hf0ffff
  // Probe on 32'hffff0f00
  // Probe on 32'hf0ffff
  ALU ALU (
    .A(32'hf0ffff), .B(32'hffff0f00), .Codop(4'b1000), .\output (ALU_output), .Flags(ALU_flags));  // open: Carry, Shift
  // Probe on ALU_output
  // Probe on ALU_output
  // Probe on ALU_flags

  // Notes on the sheet:
  //   Input A (héxa)
  //   Input B (héxa)
  //   codop
endmodule

module Test_10_0_A (
);

  wire [3:0] ALU_flags;
  wire [31:0] ALU_output;

  // Probe on 32'hfff
  // Probe on 32'hfff
  ALU ALU (.A(32'hfff), .Carry(1'b0), .Codop(4'b1001), .\output (ALU_output), .Flags(ALU_flags));  // open: B, Shift
  // Probe on ALU_output
  // Probe on ALU_output
  // Probe on ALU_flags

  // Notes on the sheet:
  //   Input A (héxa)
  //   codop
  //   carry
endmodule

module Test_11_A_B (
);

  wire [3:0] ALU_flags;
  wire [31:0] ALU_output;

  // Probe on 32'hf0f0f
  // Probe on 32'hf0f0f0f
  // Probe on 32'hf0f0f
  // Probe on 32'hf0f0f0f
  ALU ALU (
    .A(32'hf0f0f0f), .B(32'hf0f0f), .Carry(1'b0), .Codop(4'b1010), .\output (ALU_output), .Flags(ALU_flags));  // open: Shift
  // Probe on ALU_output
  // Probe on ALU_output
  // Probe on ALU_flags

  // Notes on the sheet:
  //   Input A (héxa)
  //   Input B (héxa)
  //   codop
  //   carry
endmodule

module Test_12_A_B (
);

  wire [3:0] ALU_flags;
  wire [31:0] ALU_output;

  // Probe on 32'h86
  // Probe on 32'hae
  // Probe on 32'h86
  // Probe on 32'hae
  ALU ALU (
    .A(32'hae), .B(32'h86), .Carry(1'b1), .Codop(4'b1011), .\output (ALU_output), .Flags(ALU_flags));  // open: Shift
  // Probe on ALU_output
  // Probe on ALU_output
  // Probe on ALU_flags

  // Notes on the sheet:
  //   Input A (héxa)
  //   Input B (héxa)
  //   codop
  //   carry
endmodule

module Test_13_A_OR_B (
);

  wire [3:0] ALU_flags;
  wire [31:0] ALU_output;

  // Probe on 32'hff
  // Probe on 32'hf00000a
  // Probe on 32'hff
  // Probe on 32'hf00000a
  ALU ALU (
    .A(32'hf00000a), .B(32'hff), .Codop(4'b1100), .\output (ALU_output), .Flags(ALU_flags));  // open: Carry, Shift
  // Probe on ALU_output
  // Probe on ALU_output
  // Probe on ALU_flags

  // Notes on the sheet:
  //   Input A (héxa)
  //   Input B (héxa)
  //   codop
endmodule

module Test_14_A_B (
);

  wire [3:0] ALU_flags;
  wire [31:0] ALU_output;

  // Probe on 32'ha
  // Probe on 32'h5
  // Probe on 32'ha
  // Probe on 32'h5
  ALU ALU (.A(32'h5), .B(32'ha), .Codop(4'b1101), .\output (ALU_output), .Flags(ALU_flags));  // open: Carry, Shift
  // Probe on ALU_output
  // Probe on ALU_output
  // Probe on ALU_flags

  // Notes on the sheet:
  //   Input A (héxa)
  //   Input B (héxa)
  //   codop
endmodule

module Test_15_A_AND_NOT_B (
);

  wire [3:0] ALU_flags;
  wire [31:0] ALU_output;

  // Probe on 32'hffff0f00
  // Probe on 32'hf0ffff
  // Probe on 32'hffff0f00
  // Probe on 32'hf0ffff
  ALU ALU (
    .A(32'hf0ffff), .B(32'hffff0f00), .Codop(4'b1110), .\output (ALU_output), .Flags(ALU_flags));  // open: Carry, Shift
  // Probe on ALU_output
  // Probe on ALU_output
  // Probe on ALU_flags

  // Notes on the sheet:
  //   Input A (héxa)
  //   Input B (héxa)
  //   codop
endmodule

module Test_16_NOT_B (
);

  wire [3:0] ALU_flags;
  wire [31:0] ALU_output;

  // Probe on 32'hffff
  // Probe on 32'hffff
  ALU ALU (.B(32'hffff), .Codop(4'b1111), .\output (ALU_output), .Flags(ALU_flags));  // open: A, Carry, Shift
  // Probe on ALU_output
  // Probe on ALU_output
  // Probe on ALU_flags

  // Notes on the sheet:
  //   Input B (héxa)
  //   codop
endmodule
