// Logisim project BancDeRegistre.circ as structural Verilog: 2 circuits, main circuit main
module main (
  input  [31:0] in_1,
  input  [31:0] in_2,
  input  [2:0] in_3,
  input  [2:0] in_4,
  input  [2:0] in_5,
  input  [31:0] in_6,
  input  in_7
);

  BancDeRegistre bancderegistre_1 (
    .DataIn(in_1), .RegA(in_3), .RegB(in_4), .Reset(in_7), .RegDest(in_5), .AOut(in_2), .BOut(in_6));
endmodule

module BancDeRegistre (
  input  [31:0] DataIn,
  input  [2:0] RegA,
  input  [2:0] RegB,
  input  Reset,
  input  [2:0] RegDest,
  output [31:0] AOut,
  output [31:0] BOut
);

  wire clock_1_out, demultiplexer_1_out0, demultiplexer_1_out1, demultiplexer_1_out2, demultiplexer_1_out3,
       demultiplexer_1_out4, demultiplexer_1_out5, demultiplexer_1_out6, demultiplexer_1_out7;
  wire [31:0] R0_q, R1_q, R2_q, R3_q, R4_q, R5_q, R6_q, R7_q;

  Clock clock_1 (.out(clock_1_out));
  Demultiplexer #(.select(3)) demultiplexer_1 (
    .out0(demultiplexer_1_out0), .out1(demultiplexer_1_out1), .out2(demultiplexer_1_out2),
    .out3(demultiplexer_1_out3), .out4(demultiplexer_1_out4), .out5(demultiplexer_1_out5),
    .out6(demultiplexer_1_out6), .out7(demultiplexer_1_out7), .in(1'b1), .sel(RegDest));  // open: en
  // Probe on RegDest
  Register #(.width(32)) R0 (.D(DataIn), .en(demultiplexer_1_out0), .Q(R0_q), .clk(clock_1_out), .clr(Reset));
  Register #(.width(32)) R1 (.D(DataIn), .en(demultiplexer_1_out1), .Q(R1_q), .clk(clock_1_out), .clr(Reset));
  Register #(.width(32)) R2 (.D(DataIn), .en(demultiplexer_1_out2), .Q(R2_q), .clk(clock_1_out), .clr(Reset));
  Register #(.width(32)) R3 (.D(DataIn), .en(demultiplexer_1_out3), .Q(R3_q), .clk(clock_1_out), .clr(Reset));
  Register #(.width(32)) R4 (.D(DataIn), .en(demultiplexer_1_out4), .Q(R4_q), .clk(clock_1_out), .clr(Reset));
  Register #(.width(32)) R5 (.D(DataIn), .en(demultiplexer_1_out5), .Q(R5_q), .clk(clock_1_out), .clr(Reset));
  Register #(.width(32)) R6 (.D(DataIn), .en(demultiplexer_1_out6), .Q(R6_q), .clk(clock_1_out), .clr(Reset));
  Register #(.width(32)) R7 (.D(DataIn), .en(demultiplexer_1_out7), .Q(R7_q), .clk(clock_1_out), .clr(Reset));
  Multiplexer #(.select(3), .width(32)) multiplexer_1 (
    .in0(R0_q), .in1(R1_q), .in2(R2_q), .in3(R3_q), .in4(R4_q), .in5(R5_q), .in6(R6_q), .in7(R7_q),
    .out(AOut), .sel(RegA));  // open: en
  Multiplexer #(.select(3), .width(32)) multiplexer_2 (
    .in0(R0_q), .in1(R1_q), .in2(R2_q), .in3(R3_q), .in4(R4_q), .in5(R5_q), .in6(R6_q), .in7(R7_q),
    .out(BOut), .sel(RegB));  // open: en
endmodule
