// Logisim project controller.circ as structural Verilog: 29 circuits, main circuit main
module main (
  input  [15:0] in_1,
  input  [3:0] Flags,
  input  Clk,
  input  Reset,
  output Carry,
  output DP_shift,
  output Imm32_Enable,
  output [4:0] Imm5,
  output [31:0] Imm32,
  output [3:0] ALU_OPCODE,
  output [2:0] Rm,
  output [2:0] Rn,
  output [2:0] Rd,
  output [31:0] RAM_Addr,
  output Load,
  output Store,
  output [7:0] PC
);

  wire Conditionnal_verified, Decoder_branch, Decoder_dataprocessing, Decoder_load_store, Decoder_shift,
       Decoder_sp_address, SASM_carry, SP_Address_write_enable;
  wire [2:0] Data_processing_rd, Data_processing_rm, Data_processing_rn, Load_Store_rd, Load_Store_rm,
       SASM_rd, SASM_rm, SASM_rn;
  wire [3:0] Data_processing_alu_opcode, Data_processing_flags_update_mask, flag_APSR_flag_out, or_1_out,
       SASM_alu_opcode, SASM_flags_update_mask;
  wire [5:0] extract_OPCODE_opcode;
  wire [7:0] adder_1_out, adder_2_out, Conditionnal_offset;
  wire [31:0] SP_Address_new_stack_pointer, Stack_Pointer_q;

  extract_OPCODE extract_OPCODE (.in_1(in_1), .OPCODE(extract_OPCODE_opcode));
  decoder Decoder (
    .OpCode(extract_OPCODE_opcode), .load_store(Decoder_load_store), .sp_address(Decoder_sp_address),
    .branch(Decoder_branch), .dataprocessing(Decoder_dataprocessing), .shift(Decoder_shift));
  Register #(.width(32)) Stack_Pointer (
    .D(SP_Address_new_stack_pointer), .en(SP_Address_write_enable), .Q(Stack_Pointer_q), .clk(Clk));  // open: clr
  assign or_1_out = Data_processing_flags_update_mask | SASM_flags_update_mask;  // OR_Gate or_1, 4 bits wide
  block_sasm SASM (
    .in_1(in_1), .enable(Decoder_shift), .Imm5(Imm5), .Rm(SASM_rm), .Rd(SASM_rd), .Rn(SASM_rn),
    .ALU_Opcode(SASM_alu_opcode), .Flags_Update_Mask(SASM_flags_update_mask), .Carry(SASM_carry),
    .Imm32_Enable(Imm32_Enable), .Imm32(Imm32));
  block_dataprocessing Data_processing (
    .Instruction(in_1), .enable(Decoder_dataprocessing), .ALU_OPCODE(Data_processing_alu_opcode),
    .Rn(Data_processing_rn), .Rm(Data_processing_rm), .Rd(Data_processing_rd),
    .Flags_Update_Mask(Data_processing_flags_update_mask));
  FlagAPSR flag_APSR (.Flag_In(Flags), .Update_Mask(or_1_out), .Clk(Clk), .Reset(Reset), .Flag_Out(flag_APSR_flag_out));
  Block__Load_Store Load_Store (
    .enable(Decoder_load_store), .Stack_Pointer(Stack_Pointer_q), .Clk(Clk), .Reset(Reset),
    .rm(Load_Store_rm), .rd(Load_Store_rd), .RAM_Addr(RAM_Addr), .store(Load), .load(Store));  // open: Instruction, pc_hold
  SP_Address SP_Address (
    .Instruction(in_1), .Stack_Pointer(Stack_Pointer_q), .Enable(Decoder_sp_address),
    .New_Stack_Pointer(SP_Address_new_stack_pointer), .Write_Enable(SP_Address_write_enable));
  Conditionnal Conditionnal (
    .Enable(Decoder_branch), .N(flag_APSR_flag_out[3]), .Z(flag_APSR_flag_out[2]), .C(flag_APSR_flag_out[1]),
    .V(flag_APSR_flag_out[0]), .Offset(Conditionnal_offset), .Verified(Conditionnal_verified));  // open: Instruction
  Adder adder_1 (.a(8'h3), .b(Conditionnal_offset), .out(adder_1_out), .cin(1'b0));  // open: cout
  Adder adder_2 (.a(adder_1_out), .b(PC), .out(adder_2_out));  // open: cin, cout
  and and_1 (DP_shift, ~Decoder_shift, Decoder_load_store);  // AND_Gate
  Counter counter_1 (
    .load(1'b1), .D(adder_2_out), .count(Conditionnal_verified), .Q(PC), .clk(Clk), .clr(Reset));  // open: carry
  Multiplexer #(.enable("false")) multiplexer_1 (
    .in0(flag_APSR_flag_out[1]), .in1(SASM_carry), .out(Carry), .sel(DP_shift));
  assign ALU_OPCODE = SASM_alu_opcode | Data_processing_alu_opcode;  // OR_Gate or_2, 4 bits wide
  assign Rm = SASM_rm | Data_processing_rm | Load_Store_rm;  // OR_Gate or_3, 3 bits wide
  assign Rn = SASM_rn | Data_processing_rn;  // OR_Gate or_4, 3 bits wide
  assign Rd = SASM_rd | Data_processing_rd | Load_Store_rd;  // OR_Gate or_5, 3 bits wide

  // Other names for the same wires on the sheet: bin[15:0] = in_1

  // Notes on the sheet:
  //   Extract carry
endmodule

module decoder (
  input  [5:0] OpCode,
  output load_store,
  output sp_address,
  output branch,
  output dataprocessing,
  output shift
);

  wire not_1_out, not_2_out, not_3_out, not_4_out, not_5_out, not_6_out, not_7_out, not_8_out, not_9_out;

  not not_1 (not_1_out, OpCode[3]);
  not not_2 (not_2_out, OpCode[3]);
  not not_3 (not_3_out, OpCode[0]);
  not not_4 (not_4_out, OpCode[1]);
  not not_5 (not_5_out, OpCode[2]);
  and and_1 (dataprocessing, not_3_out, not_4_out, not_5_out, not_6_out, OpCode[4], not_7_out);
  not not_6 (not_6_out, OpCode[3]);
  not not_7 (not_7_out, OpCode[5]);
  nor nor_1 (shift, OpCode[4], OpCode[5]);
  not not_8 (not_8_out, OpCode[4]);
  not not_9 (not_9_out, OpCode[4]);
  and and_2 (branch, OpCode[2], not_2_out, OpCode[4], OpCode[5]);
  and and_3 (load_store, OpCode[2], not_1_out, not_8_out, OpCode[5]);
  and and_4 (sp_address, OpCode[5], OpCode[2], OpCode[3], not_9_out);
endmodule

module block_dataprocessing (
  input  [15:0] Instruction,
  input  enable,
  output [3:0] ALU_OPCODE,
  output [2:0] Rn,
  output [2:0] Rm,
  output [2:0] Rd,
  output [3:0] Flags_Update_Mask
);

  wire ADC, AND, ASR, BIC, CMN, CMP, EOR, LSL, LSR, MUL, MVN, NULL, or_1_out, or_2_out, ORR, ROR, RSB, SBC,
       TST;
  wire [3:0] multiplexer_2_out, multiplexer_3_out, multiplexer_4_out, or_3_out;
  wire [15:0] multiplexer_1_out;

  Multiplexer #(.width(16), .enable("false")) multiplexer_1 (
    .in0({16{1'b0}}), .in1(Instruction), .out(multiplexer_1_out), .sel(enable));
  extract_dataP Extract_all_dataP (
    .in_1(multiplexer_1_out), .out_3(ALU_OPCODE), .out_4(Rd), .out_5(Rm));  // open: out_2
  or or_1 (or_1_out, AND, EOR, LSL, LSR, ASR, ROR, TST, ORR, BIC, MVN);
  or or_2 (or_2_out, ADC, SBC, RSB, CMP, CMN);
  decoder_dataP Decoder_dataP (
    .in_1(multiplexer_1_out), .enable(enable), .NULL(NULL), .AND(AND), .EOR(EOR), .LSL(LSL), .LSR(LSR),
    .ASR(ASR), .ADC(ADC), .SBC(SBC), .ROR(ROR), .TST(TST), .RSB(RSB), .CMP(CMP), .CMN(CMN), .ORR(ORR),
    .MUL(MUL), .BICC(BIC), .MVN(MVN));
  Multiplexer #(.width(4), .enable("false")) multiplexer_2 (
    .in0(4'b0000), .in1(4'b1100), .out(multiplexer_2_out), .sel(MUL));
  Multiplexer #(.width(4), .enable("false")) multiplexer_3 (
    .in0(4'b0000), .in1(4'b1110), .out(multiplexer_3_out), .sel(or_1_out));
  Multiplexer #(.width(4), .enable("false")) multiplexer_4 (
    .in0(4'b0000), .in1(4'b1111), .out(multiplexer_4_out), .sel(or_2_out));
  assign or_3_out = multiplexer_2_out | multiplexer_3_out | multiplexer_4_out;  // OR_Gate or_3, 4 bits wide
  Multiplexer #(.width(4), .enable("false")) multiplexer_5 (
    .in0(or_3_out), .in1(4'b0000), .out(Flags_Update_Mask), .sel(NULL));

  assign Rn = Rd;

  // Notes on the sheet:
  //   Flags
  //   N Z
  //   N Z C
  //   N Z C V
  //   N Z C V
endmodule

module extract_dataP (
  input  [15:0] in_1,
  output [5:0] out_2,
  output [3:0] out_3,
  output [2:0] out_4,
  output [2:0] out_5
);

  BitSelector #(.width(16), .group(2)) bitselector_1 (.in(in_1), .out(out_2[1:0]), .sel(3'b101));
  BitSelector #(.width(16), .group(2)) bitselector_2 (.in(in_1), .out(out_2[3:2]), .sel(3'b110));
  BitSelector #(.width(16), .group(2)) bitselector_3 (.in(in_1), .out(out_2[5:4]), .sel(3'b111));
  BitSelector #(.width(16), .group(2)) bitselector_4 (.in(in_1), .out(out_3[1:0]), .sel(3'b011));
  BitSelector #(.width(16), .group(2)) bitselector_5 (.in(in_1), .out(out_3[3:2]), .sel(3'b100));
  BitSelector #(.width(16), .group(3)) bitselector_6 (.in(in_1), .out(out_4), .sel(3'b001));
  BitSelector #(.width(16), .group(3)) bitselector_7 (.in(in_1), .out(out_5), .sel(3'b000));
endmodule

module extract_LogicalShift (
  input  [15:0] in_1,
  output [2:0] out_2,
  output [1:0] out_3,
  output [4:0] out_4,
  output [2:0] out_5,
  output [2:0] out_6
);

  BitSelector #(.width(16), .group(2)) bitselector_1 (.in(in_1), .out({out_2[0], out_3[1]}), .sel(3'b110));
  BitSelector #(.width(16), .group(2)) bitselector_2 (.in(in_1), .out(out_2[2:1]), .sel(3'b111));
  BitSelector #(.width(16)) bitselector_3 (.in(in_1), .out(out_3[0]), .sel(4'b1011));
  BitSelector #(.width(16), .group(2)) bitselector_4 (.in(in_1), .out(out_4[1:0]), .sel(3'b011));
  BitSelector #(.width(16), .group(2)) bitselector_5 (.in(in_1), .out(out_4[3:2]), .sel(3'b100));
  BitSelector #(.width(16)) bitselector_6 (.in(in_1), .out(out_4[4]), .sel(4'b1010));
  BitSelector #(.width(16), .group(3)) bitselector_7 (.in(in_1), .out(out_5), .sel(3'b001));
  BitSelector #(.width(16), .group(3)) bitselector_8 (.in(in_1), .out(out_6), .sel(3'b000));
endmodule

module extract_addSub (
  input  [15:0] in_1,
  output [2:0] out_2,
  output [1:0] out_3,
  output out_4,
  output out_5,
  output [2:0] out_6,
  output [2:0] out_7,
  output [2:0] out_8
);

  BitSelector #(.width(16), .group(2)) bitselector_1 (.in(in_1), .out({out_2[0], out_3[1]}), .sel(3'b110));
  BitSelector #(.width(16), .group(2)) bitselector_2 (.in(in_1), .out(out_2[2:1]), .sel(3'b111));
  BitSelector #(.width(16)) bitselector_3 (.in(in_1), .out(out_3[0]), .sel(4'b1011));
  BitSelector #(.width(16), .group(2)) bitselector_4 (.in(in_1), .out(out_6[1:0]), .sel(3'b011));
  BitSelector #(.width(16), .group(2)) bitselector_5 (.in(in_1), .out({out_5, out_6[2]}), .sel(3'b100));
  BitSelector #(.width(16)) bitselector_6 (.in(in_1), .out(out_4), .sel(4'b1010));
  BitSelector #(.width(16), .group(3)) bitselector_7 (.in(in_1), .out(out_7), .sel(3'b001));
  BitSelector #(.width(16), .group(3)) bitselector_8 (.in(in_1), .out(out_8), .sel(3'b000));
endmodule

module block_sasm (
  input  [15:0] in_1,
  input  enable,
  output [4:0] Imm5,
  output [2:0] Rm,
  output [2:0] Rd,
  output [2:0] Rn,
  output [3:0] ALU_Opcode,
  output [3:0] Flags_Update_Mask,
  output Carry,
  output Imm32_Enable,
  output [31:0] Imm32
);

  wire ADD, ADD_register, ASR, decoderSASM_lsl, decoderSASM_null, LSL, LSR, MOV, nand_1_out, or_1_out,
       or_2_out, or_3_out, or_4_out, or_8_out, or_9_out, or_10_out, SUB, SUB_register;
  wire [2:0] Add_Sub__immediate_out_7, Add_Sub__immediate_out_8, Add_Sub__register_out_6,
       Add_Sub__register_out_7, Add_Sub__register_out_8, imm3, LSL_LSR_ASR_out_5, LSL_LSR_ASR_out_6, Mov_rd;
  wire [3:0] multiplexer_10_out, multiplexer_11_out, multiplexer_12_out;
  wire [7:0] imm8;
  wire [15:0] multiplexer_1_out, multiplexer_3_out, multiplexer_4_out, multiplexer_5_out, multiplexer_6_out;
  wire [31:0] multiplexer_7_out, multiplexer_8_out;

  Multiplexer #(.width(16), .enable("false")) multiplexer_1 (
    .in0({16{1'b0}}), .in1(in_1), .out({multiplexer_1_out[15:14], ALU_Opcode, multiplexer_1_out[9:0]}),
    .sel(enable));
  decoder_sasm decoderSASM (
    .in_1({multiplexer_1_out[15:14], ALU_Opcode, multiplexer_1_out[9:0]}), .enable(enable),
    .NULL(decoderSASM_null), .LSL(decoderSASM_lsl), .LSR(LSR), .ASR(ASR), .ADD_register(ADD_register),
    .SUB_register(SUB_register), .ADD(ADD), .SUB(SUB), .MOV(MOV));
  Multiplexer #(.enable("false")) multiplexer_2 (.in0(decoderSASM_lsl), .in1(1'b0), .out(LSL), .sel(decoderSASM_null));
  Multiplexer #(.width(16), .enable("false")) multiplexer_3 (
    .in0({16{1'b0}}), .in1(in_1), .out(multiplexer_3_out), .sel(or_3_out));
  Multiplexer #(.width(16), .enable("false")) multiplexer_4 (
    .in0({16{1'b0}}), .in1(in_1), .out(multiplexer_4_out), .sel(or_1_out));
  or or_1 (or_1_out, ADD_register, SUB_register);
  Multiplexer #(.width(16), .enable("false")) multiplexer_5 (
    .in0({16{1'b0}}), .in1(in_1), .out(multiplexer_5_out), .sel(or_2_out));
  or or_2 (or_2_out, ADD, SUB);
  Multiplexer #(.width(16), .enable("false")) multiplexer_6 (
    .in0({16{1'b0}}), .in1(in_1), .out(multiplexer_6_out), .sel(MOV));
  extract_LogicalShift LSL_LSR_ASR (
    .in_1(multiplexer_3_out), .out_4(Imm5), .out_5(LSL_LSR_ASR_out_5), .out_6(LSL_LSR_ASR_out_6));  // open: out_2, out_3
  or or_3 (or_3_out, LSL, LSR, ASR);
  extract_addSub Add_Sub__register (
    .in_1(multiplexer_4_out), .out_6(Add_Sub__register_out_6), .out_7(Add_Sub__register_out_7),
    .out_8(Add_Sub__register_out_8));  // open: out_2, out_3, out_4, out_5
  extract_addSub Add_Sub__immediate (
    .in_1(multiplexer_5_out), .out_6(imm3), .out_7(Add_Sub__immediate_out_7), .out_8(Add_Sub__immediate_out_8));  // open: out_2, out_3, out_4, out_5
  extract_mov_Immediate u_Mov (.in_1(multiplexer_6_out), .imm8(imm8), .Rd(Mov_rd));
  or or_4 (or_4_out, ADD, SUB);
  Multiplexer #(.width(32), .enable("false")) multiplexer_7 (
    .in0({32{1'b0}}), .in1({{29{1'b0}}, imm3}), .out(multiplexer_7_out), .sel(or_4_out));
  Multiplexer #(.width(32), .enable("false")) multiplexer_8 (
    .in0({32{1'b0}}), .in1({{24{1'b0}}, imm8}), .out(multiplexer_8_out), .sel(MOV));
  assign Rm = LSL_LSR_ASR_out_5 | Add_Sub__register_out_8 | Add_Sub__immediate_out_8;  // OR_Gate or_5, 3 bits wide
  assign Rd = LSL_LSR_ASR_out_6 | Add_Sub__register_out_6 | Mov_rd;  // OR_Gate or_6, 3 bits wide
  assign Rn = Add_Sub__register_out_7 | Add_Sub__immediate_out_7;  // OR_Gate or_7, 3 bits wide
  nand nand_1 (nand_1_out, or_4_out, 1'b1);
  or or_8 (or_8_out, nand_1_out, MOV);
  Multiplexer #(.width(32), .enable("false")) multiplexer_9 (
    .in0(multiplexer_7_out), .in1(multiplexer_8_out), .out(Imm32), .sel(or_8_out));
  or or_9 (or_9_out, LSL, LSR, ASR);
  or or_10 (or_10_out, SUB_register, ADD_register, ADD, SUB);
  Multiplexer #(.width(4), .enable("false")) multiplexer_10 (
    .in0(4'b0000), .in1(4'b1011), .out(multiplexer_10_out), .sel(MOV));
  Multiplexer #(.width(4), .enable("false")) multiplexer_11 (
    .in0(4'b0000), .in1(4'b1110), .out(multiplexer_11_out), .sel(or_9_out));
  Multiplexer #(.width(4), .enable("false")) multiplexer_12 (
    .in0(4'b0000), .in1(4'b1111), .out(multiplexer_12_out), .sel(or_10_out));
  assign Flags_Update_Mask = multiplexer_10_out | multiplexer_11_out | multiplexer_12_out;  // OR_Gate or_11, 4 bits wide
  Multiplexer #(.select(2), .enable("false")) multiplexer_13 (
    .in0(1'b0), .in2(1'b1), .out(Carry), .sel({SUB, ADD}));  // open: in1, in3
  or or_12 (Imm32_Enable, ADD, SUB, MOV);

  // Other names for the same wires on the sheet: bin[15:0] = in_1; FlagUpdateMask[3:0] = Flags_Update_Mask;
  //   Opcode[3:0] = ALU_Opcode

  // Notes on the sheet:
  //   Imm32 
  //   Imm and registers
  //   Flags
endmodule

module decoder_sasm (
  input  [15:0] in_1,
  input  enable,
  output NULL,
  output LSL,
  output LSR,
  output ASR,
  output ADD_register,
  output SUB_register,
  output ADD,
  output SUB,
  output MOV
);

  wire _00, _01, _10, extract_addsub_1_out_4, extract_addsub_1_out_5, not_3_out, not_4_out, not_5_out,
       not_6_out, not_7_out, not_8_out, not_9_out, not_10_out;
  wire [1:0] _11, extract_addsub_1_out_3;
  wire [2:0] _000, _001, extract_addsub_1_out_2, not_1_out, not_2_out;
  wire [15:0] multiplexer_1_out;

  Multiplexer #(.width(16), .enable("false")) multiplexer_1 (
    .in0({16{1'b0}}), .in1(in_1), .out(multiplexer_1_out), .sel(enable));
  extract_addSub extract_addsub_1 (
    .in_1(multiplexer_1_out), .out_2(extract_addsub_1_out_2), .out_3(extract_addsub_1_out_3),
    .out_4(extract_addsub_1_out_4), .out_5(extract_addsub_1_out_5));  // open: out_6, out_7, out_8
  assign not_1_out = ~extract_addsub_1_out_2;  // NOT_Gate not_1, 3 bits wide
  assign not_2_out = ~extract_addsub_1_out_2;  // NOT_Gate not_2, 3 bits wide
  not not_3 (not_3_out, extract_addsub_1_out_3[1]);
  not not_4 (not_4_out, extract_addsub_1_out_3[0]);
  not not_5 (not_5_out, extract_addsub_1_out_3[0]);
  not not_6 (not_6_out, extract_addsub_1_out_3[1]);
  assign _001 = 3'b001 ^ not_1_out;  // XOR_Gate xor_1, 3 bits wide
  assign _000 = 3'b111 & not_2_out;  // AND_Gate and_1, 3 bits wide
  and and_2 (_01, extract_addsub_1_out_3[0], not_3_out);
  and and_3 (_10, not_4_out, extract_addsub_1_out_3[1]);
  assign _11 = 2'b11 & extract_addsub_1_out_3;  // AND_Gate and_4, 2 bits wide
  and and_5 (_00, not_5_out, not_6_out);
  not not_7 (not_7_out, extract_addsub_1_out_5);
  not not_8 (not_8_out, extract_addsub_1_out_4);
  not not_9 (not_9_out, extract_addsub_1_out_5);
  not not_10 (not_10_out, extract_addsub_1_out_4);
  and and_6 (SUB_register, _000[0], _000[1], _000[2], _11[0], _11[1], extract_addsub_1_out_5, not_10_out);
  and and_7 (ADD, _000[0], _000[1], _000[2], _11[0], _11[1], not_9_out, extract_addsub_1_out_4);
  and and_8 (SUB, _000[0], _000[1], _000[2], _11[0], _11[1], extract_addsub_1_out_5, extract_addsub_1_out_4);
  and and_9 (MOV, _001[0], _001[2], _00);
  and and_10 (LSL, _000[0], _000[1], _000[2], _00);
  and and_11 (LSR, _000[0], _000[2], _01);
  and and_12 (ASR, _000[0], _000[2], _10);
  and and_13 (ADD_register, _000[0], _000[1], _000[2], _11[1], not_7_out, not_8_out);
  not not_11 (NULL, enable);
endmodule

module extract_mov_Immediate (
  input  [15:0] in_1,
  output [7:0] imm8,
  output [2:0] Rd
);

  wire [3:3] bitselector_2_out;

  BitSelector #(.width(16), .group(8)) bitselector_1 (.in(in_1), .out(imm8), .sel(1'b0));
  BitSelector #(.width(16), .group(4)) bitselector_2 (.in(in_1), .out({bitselector_2_out[3], Rd}), .sel(2'b10));
endmodule

module extract_OPCODE (
  input  [15:0] in_1,
  output [5:0] OPCODE
);

  BitSelector #(.width(16), .group(4)) bitselector_1 (.in(in_1), .out(OPCODE[5:2]), .sel(2'b11));
  BitSelector #(.width(16), .group(2)) bitselector_2 (.in(in_1), .out(OPCODE[1:0]), .sel(3'b101));
endmodule

module Block__Load_Store (
  input  [15:0] Instruction,
  input  enable,
  input  [31:0] Stack_Pointer,
  input  Clk,
  input  Reset,
  output [2:0] rm,
  output [2:0] rd,
  output [31:0] RAM_Addr,
  output store,
  output load,
  output pc_hold
);

  wire and_1_out, and_2_out, and_3_out, Dload, LDR_STR, Load_t, not_1_out;
  wire [2:0] rt;
  wire [7:0] bitselector_1_out, bitselector_2_out;
  wire [15:0] multiplexer_1_out;
  wire [31:0] adder_1_out, bit_extender_1_out;

  and and_1 (and_1_out, Dload, LDR_STR);
  Multiplexer #(.width(16), .enable("false")) multiplexer_1 (
    .in0({16{1'b0}}), .in1(Instruction), .out(multiplexer_1_out), .sel(enable));
  BitSelector #(.width(16), .group(8)) bitselector_1 (.in(multiplexer_1_out), .out(bitselector_1_out), .sel(1'b0));
  BitSelector #(.width(16), .group(8)) bitselector_2 (.in(multiplexer_1_out), .out(bitselector_2_out), .sel(1'b1));
  D_Flip_Flop d_ff_1 (.clk(Clk), .D(and_1_out), .Q(Load_t), .Qn(Dload), .preset(1'b0), .reset(Reset));  // open: en
  BitSelector #(.group(3)) bitselector_3 (.in(bitselector_2_out), .out(rt), .sel(2'b11));
  BitSelector bitselector_4 (.in(bitselector_2_out), .out(LDR_STR), .sel(3'b011));
  assign bit_extender_1_out = {{24{1'b0}}, bitselector_1_out};  // Bit_Extender bit_extender_1
  Adder #(.width(32)) adder_1 (.a(bit_extender_1_out), .b(Stack_Pointer), .out(adder_1_out));  // open: cin, cout
  Multiplexer #(.width(32), .enable("false")) multiplexer_2 (
    .in0({32{1'b0}}), .in1(adder_1_out), .out(RAM_Addr), .sel(enable));
  Multiplexer #(.width(3), .enable("false")) multiplexer_3 (.in0(3'b000), .in1(rt), .out(rd), .sel(enable));
  and and_2 (and_2_out, LDR_STR, 1'b1);
  and and_3 (and_3_out, LDR_STR, 1'b1);
  Multiplexer #(.enable("false")) multiplexer_4 (.in0(1'b0), .in1(not_1_out), .out(store), .sel(enable));
  not not_1 (not_1_out, and_2_out);
  Multiplexer #(.enable("false")) multiplexer_5 (.in0(1'b0), .in1(and_3_out), .out(load), .sel(enable));
  Multiplexer #(.enable("false")) multiplexer_6 (.in0(1'b0), .in1(Dload), .out(pc_hold), .sel(enable));

  assign rm = rd;

  // Other names for the same wires on the sheet: bin[15:0] = Instruction
endmodule

module Conditionnal (
  input  [15:0] Instruction,
  input  Enable,
  input  N,
  input  Z,
  input  C,
  input  V,
  output [7:0] Offset,
  output Verified
);

  wire and_2_out, comparator_3_eq, comparator_4_eq, comparator_5_eq, comparator_6_eq, comparator_7_eq,
       comparator_8_eq, comparator_9_eq, EQ, HI, LS, NE, not_1_out, or_1_out;
  wire [3:0] Cond;

  BitSelector #(.width(16), .group(4)) bitselector_1 (.in(Instruction), .out(Cond), .sel(2'b10));
  BitSelector #(.width(16), .group(8)) bitselector_2 (.in(Instruction), .out(Offset), .sel(1'b0));
  Comparator #(.width(1)) comparator_1 (.a(Z), .b(1'b1), .eq(EQ));  // open: gt, lt
  Comparator #(.width(1)) comparator_2 (.a(Z), .b(1'b0), .eq(NE));  // open: gt, lt
  Comparator #(.width(1)) comparator_3 (.a(C), .b(1'b1), .eq(comparator_3_eq));  // open: gt, lt
  Comparator #(.width(1)) comparator_4 (.a(C), .b(1'b0), .eq(comparator_4_eq));  // open: gt, lt
  Comparator #(.width(1)) comparator_5 (.a(N), .b(1'b1), .eq(comparator_5_eq));  // open: gt, lt
  Comparator #(.width(1)) comparator_6 (.a(N), .b(1'b0), .eq(comparator_6_eq));  // open: gt, lt
  Comparator #(.width(1)) comparator_7 (.a(V), .b(1'b1), .eq(comparator_7_eq));  // open: gt, lt
  Comparator #(.width(1)) comparator_8 (.a(V), .b(1'b0), .eq(comparator_8_eq));  // open: gt, lt
  Comparator #(.width(1)) comparator_9 (.a(N), .b(V), .eq(comparator_9_eq));  // open: gt, lt
  not not_1 (not_1_out, comparator_9_eq);
  and and_1 (HI, NE, comparator_3_eq);
  or or_1 (or_1_out, not_1_out, EQ);
  and and_2 (and_2_out, comparator_9_eq, NE);
  // Probe on not_1_out
  or or_2 (LS, NE, comparator_3_eq);
  Multiplexer #(.select(4)) multiplexer_1 (
    .in0(EQ), .in1(NE), .in2(comparator_3_eq), .in3(comparator_4_eq), .in4(comparator_5_eq),
    .in5(comparator_6_eq), .in6(comparator_7_eq), .in7(comparator_8_eq), .in8(HI), .in9(LS),
    .in10(comparator_9_eq), .in11(not_1_out), .in12(and_2_out), .in13(or_1_out), .in14(1'b1), .out(Verified),
    .sel(Cond), .en(Enable));  // open: in15
endmodule

module FlagAPSR (
  input  [3:0] Flag_In,
  input  [3:0] Update_Mask,
  input  Clk,
  input  Reset,
  output [3:0] Flag_Out
);

  Register #(.width(1)) register_1 (.D(Flag_In[0]), .en(Update_Mask[0]), .Q(Flag_Out[0]), .clk(Clk), .clr(Reset));
  Register #(.width(1)) register_2 (.D(Flag_In[1]), .en(Update_Mask[1]), .Q(Flag_Out[1]), .clk(Clk), .clr(Reset));
  Register #(.width(1)) register_3 (.D(Flag_In[2]), .en(Update_Mask[2]), .Q(Flag_Out[2]), .clk(Clk), .clr(Reset));
  Register #(.width(1)) register_4 (.D(Flag_In[3]), .en(Update_Mask[3]), .Q(Flag_Out[3]), .clk(Clk), .clr(Reset));
endmodule

module SP_Address (
  input  [15:0] Instruction,
  input  [31:0] Stack_Pointer,
  input  Enable,
  output [31:0] New_Stack_Pointer,
  output Write_Enable
);

  wire comparator_1_eq;
  wire [6:0] adder_1_out, bitselector_1_out, subtractor_1_out;

  BitSelector #(.width(16), .group(7)) bitselector_1 (.in(Instruction), .out(bitselector_1_out), .sel(2'b00));
  Subtractor #(.width(7)) subtractor_1 (
    .a(Stack_Pointer[6:0]), .b(bitselector_1_out), .out(subtractor_1_out));  // open: bin, bout
  Adder #(.width(7)) adder_1 (.a(bitselector_1_out), .b(Stack_Pointer[6:0]), .out(adder_1_out));  // open: cin, cout
  Comparator #(.width(1)) comparator_1 (.a(Instruction[7]), .b(1'b0), .eq(comparator_1_eq));  // open: gt, lt
  Multiplexer #(.width(7)) multiplexer_1 (
    .in0(subtractor_1_out), .in1(adder_1_out), .out(New_Stack_Pointer[6:0]), .sel(comparator_1_eq),
    .en(Enable));

  assign New_Stack_Pointer[31:7] = Stack_Pointer[31:7];
  assign Write_Enable = Enable;
endmodule

module Program_counter (
  input  [7:0] Data,
  input  Count,
  input  UpDown,
  input  Load,
  input  Clk,
  input  Clear,
  output [7:0] Output,
  output Carry
);

  wire [0:0] not_1_out;
  wire [7:0] adder_1_out, demultiplexer_1_out0, demultiplexer_1_out1, demultiplexer_1_out2,
       demultiplexer_1_out3, multiplexer_1_out, register_1_q, subtractor_1_out;

  not not_1 (not_1_out[0], UpDown);
  Multiplexer #(.width(8)) multiplexer_1 (.in0(Output), .in1(Data), .out(multiplexer_1_out), .sel(Load));  // open: en
  Register register_1 (.D(multiplexer_1_out), .Q(register_1_q), .clk(Clk), .clr(Clear));  // open: en
  Demultiplexer #(.select(2), .width(8)) demultiplexer_1 (
    .out0(demultiplexer_1_out0), .out1(demultiplexer_1_out1), .out2(demultiplexer_1_out2),
    .out3(demultiplexer_1_out3), .in(register_1_q), .sel({Count, not_1_out[0]}));  // open: en
  Adder adder_1 (.a(demultiplexer_1_out2), .b(8'h1), .out(adder_1_out));  // open: cin, cout
  Subtractor subtractor_1 (.a(demultiplexer_1_out3), .b(8'h1), .out(subtractor_1_out));  // open: bin, bout
  Multiplexer #(.select(2), .width(8)) multiplexer_2 (
    .in0(demultiplexer_1_out0), .in1(demultiplexer_1_out1), .in2(adder_1_out), .in3(subtractor_1_out),
    .out(Output), .sel({Count, not_1_out[0]}));  // open: en
endmodule

module decoder_dataP (
  input  [15:0] in_1,
  input  enable,
  output NULL,
  output AND,
  output EOR,
  output LSL,
  output LSR,
  output ASR,
  output ADC,
  output SBC,
  output ROR,
  output TST,
  output RSB,
  output CMP,
  output CMN,
  output ORR,
  output MUL,
  output BICC,
  output MVN
);

  wire _010000, comparator_1_gt, comparator_1_lt, not_1_out, not_2_out, not_3_out, not_4_out, not_5_out,
       not_6_out, not_7_out, not_8_out, not_9_out, not_10_out, not_11_out, not_12_out, not_13_out,
       not_14_out, not_15_out, not_16_out, not_17_out, not_18_out, not_19_out, not_20_out, not_21_out,
       not_22_out, not_23_out, not_24_out, not_25_out, not_26_out, not_27_out, not_28_out, not_29_out,
       not_30_out, not_31_out, not_32_out;
  wire [3:0] ExtracteurDataP_out_3, multiplexer_2_out;
  wire [5:0] ExtracteurDataP_out_2;
  wire [15:0] multiplexer_1_out;

  Multiplexer #(.width(16), .enable("false")) multiplexer_1 (
    .in0({16{1'b0}}), .in1(in_1), .out(multiplexer_1_out), .sel(enable));
  extract_dataP ExtracteurDataP (
    .in_1(multiplexer_1_out), .out_2(ExtracteurDataP_out_2), .out_3(ExtracteurDataP_out_3));  // open: out_4, out_5
  Multiplexer #(.width(4), .enable("false")) multiplexer_2 (
    .in0(4'b0000), .in1(ExtracteurDataP_out_3), .out(multiplexer_2_out), .sel(_010000));
  Comparator #(.width(6)) comparator_1 (
    .a(6'b010000), .b(ExtracteurDataP_out_2), .gt(comparator_1_gt), .eq(_010000), .lt(comparator_1_lt));
  not not_1 (not_1_out, multiplexer_2_out[1]);
  not not_2 (not_2_out, multiplexer_2_out[0]);
  or or_1 (NULL, comparator_1_gt, comparator_1_lt);
  not not_3 (not_3_out, multiplexer_2_out[3]);
  not not_4 (not_4_out, multiplexer_2_out[2]);
  not not_5 (not_5_out, multiplexer_2_out[1]);
  not not_6 (not_6_out, multiplexer_2_out[0]);
  not not_7 (not_7_out, multiplexer_2_out[3]);
  not not_8 (not_8_out, multiplexer_2_out[2]);
  not not_9 (not_9_out, multiplexer_2_out[1]);
  not not_10 (not_10_out, multiplexer_2_out[3]);
  not not_11 (not_11_out, multiplexer_2_out[2]);
  not not_12 (not_12_out, multiplexer_2_out[0]);
  not not_13 (not_13_out, multiplexer_2_out[3]);
  not not_14 (not_14_out, multiplexer_2_out[2]);
  not not_15 (not_15_out, multiplexer_2_out[3]);
  not not_16 (not_16_out, multiplexer_2_out[1]);
  not not_17 (not_17_out, multiplexer_2_out[0]);
  not not_18 (not_18_out, multiplexer_2_out[3]);
  not not_19 (not_19_out, multiplexer_2_out[1]);
  not not_20 (not_20_out, multiplexer_2_out[3]);
  not not_21 (not_21_out, multiplexer_2_out[0]);
  not not_22 (not_22_out, multiplexer_2_out[3]);
  not not_23 (not_23_out, multiplexer_2_out[2]);
  not not_24 (not_24_out, multiplexer_2_out[1]);
  not not_25 (not_25_out, multiplexer_2_out[0]);
  not not_26 (not_26_out, multiplexer_2_out[2]);
  not not_27 (not_27_out, multiplexer_2_out[2]);
  not not_28 (not_28_out, multiplexer_2_out[2]);
  not not_29 (not_29_out, multiplexer_2_out[1]);
  not not_30 (not_30_out, multiplexer_2_out[0]);
  not not_31 (not_31_out, multiplexer_2_out[1]);
  not not_32 (not_32_out, multiplexer_2_out[0]);
  and and_1 (AND, not_3_out, not_4_out, not_5_out, not_6_out);
  and and_2 (EOR, not_7_out, not_8_out, not_9_out, multiplexer_2_out[0]);
  and and_3 (LSL, not_10_out, not_11_out, multiplexer_2_out[1], not_12_out);
  and and_4 (LSR, not_13_out, not_14_out, multiplexer_2_out[1], multiplexer_2_out[0]);
  and and_5 (ASR, not_15_out, multiplexer_2_out[2], not_16_out, not_17_out);
  and and_6 (ADC, not_18_out, multiplexer_2_out[2], not_19_out, multiplexer_2_out[0]);
  and and_7 (SBC, not_20_out, multiplexer_2_out[2], multiplexer_2_out[1], not_21_out);
  and and_8 (ROR, not_22_out, multiplexer_2_out[2], multiplexer_2_out[1], multiplexer_2_out[0]);
  and and_9 (TST, multiplexer_2_out[3], not_23_out, not_24_out, not_25_out);
  and and_10 (RSB, multiplexer_2_out[3], not_26_out, not_1_out, multiplexer_2_out[0]);
  and and_11 (CMP, multiplexer_2_out[3], not_27_out, multiplexer_2_out[1], not_2_out);
  and and_12 (CMN, multiplexer_2_out[3], not_28_out, multiplexer_2_out[1], multiplexer_2_out[0]);
  and and_13 (ORR, multiplexer_2_out[3], multiplexer_2_out[2], not_29_out, not_30_out);
  and and_14 (MUL, multiplexer_2_out[3], multiplexer_2_out[2], not_31_out, multiplexer_2_out[0]);
  and and_15 (BICC, multiplexer_2_out[3], multiplexer_2_out[2], multiplexer_2_out[1], not_32_out);
  and and_16 (MVN, multiplexer_2_out[3], multiplexer_2_out[2], multiplexer_2_out[1], multiplexer_2_out[0]);

  // Notes on the sheet:
  //   0000
  //   0001
  //   0010
  //   0011
  //   ...
  //   1111
endmodule

module Test_dataP (
);

  wire [2:0] DATAP_rd, DATAP_rm, DATAP_rn;
  wire [3:0] DATAP_alu_opcode, DATAP_flags_update_mask;

  // Probe on 16'h4032
  block_dataprocessing DATAP (
    .Instruction(16'h4032), .enable(1'b1), .ALU_OPCODE(DATAP_alu_opcode), .Rn(DATAP_rn), .Rm(DATAP_rm),
    .Rd(DATAP_rd), .Flags_Update_Mask(DATAP_flags_update_mask));
  // Probe on DATAP_alu_opcode
  // Probe on DATAP_flags_update_mask
  // Probe on DATAP_rn
  // Probe on DATAP_rm
  // Probe on DATAP_rd

  // Notes on the sheet:
  //   ALU_OPCODE
  //   Flag Update mask
  //   Rn
  //   Rm
  //   Rd
endmodule

module Test_sasm (
);

  wire SASM_carry, SASM_imm32_enable;
  wire [2:0] SASM_rd, SASM_rm, SASM_rn;
  wire [3:0] SASM_alu_opcode, SASM_flags_update_mask;
  wire [4:0] SASM_imm5;
  wire [31:0] SASM_imm32;

  // Probe on 16'h16af
  block_sasm SASM (
    .in_1(16'h16af), .enable(1'b1), .Imm5(SASM_imm5), .Rm(SASM_rm), .Rd(SASM_rd), .Rn(SASM_rn),
    .ALU_Opcode(SASM_alu_opcode), .Flags_Update_Mask(SASM_flags_update_mask), .Carry(SASM_carry),
    .Imm32_Enable(SASM_imm32_enable), .Imm32(SASM_imm32));
  // Probe on SASM_imm5
  // Probe on SASM_alu_opcode
  // Probe on SASM_flags_update_mask
  // Probe on SASM_carry
  // Probe on SASM_imm32_enable
  // Probe on SASM_imm32
  // Probe on SASM_rm
  // Probe on SASM_rd
  // Probe on SASM_rn

  // Notes on the sheet:
  //   Imm5
  //   ALU_OPCODE
  //   Carry
  //   Rm
  //   Flag Update mask
  //   Imm32_enable
  //   Rn
  //   Rd
endmodule

module Test_Conditional1 (
  output Verified
);

  Conditionnal conditionnal_1 (
    .Instruction({16{1'b0}}), .Enable(1'b1), .N(1'b0), .Z(1'b1), .C(1'b0), .V(1'b0), .Verified(Verified));  // open: Offset

  // Notes on the sheet:
  //   Z==1
endmodule

module Test_Conditional2 (
  output Verified
);

  Conditionnal conditionnal_1 (
    .Instruction({16{1'b0}}), .Enable(1'b1), .N(1'b0), .Z(1'b0), .C(1'b0), .V(1'b0), .Verified(Verified));  // open: Offset
endmodule

module Test_Conditional3 (
  output Verified
);

  Conditionnal conditionnal_1 (
    .Instruction(16'h200), .Enable(1'b1), .N(1'b0), .Z(1'b0), .C(1'b1), .V(1'b0), .Verified(Verified));  // open: Offset

  // Notes on the sheet:
  //   C==1
endmodule

module Test_Conditional4 (
  output Verified,
  output Verified_2
);

  Conditionnal conditionnal_1 (
    .Instruction(16'ha00), .Enable(1'b1), .N(1'b0), .Z(1'b0), .C(1'b0), .V(1'b0), .Verified(Verified));  // open: Offset
  Conditionnal conditionnal_2 (
    .Instruction(16'ha00), .Enable(1'b1), .N(1'b1), .Z(1'b0), .C(1'b0), .V(1'b0), .Verified(Verified_2));  // open: Offset

  // Notes on the sheet:
  //   N==V
endmodule

module Test_Conditional5 (
  output Verified,
  output Verified_2,
  output Verified_3
);

  Conditionnal conditionnal_1 (
    .Instruction(16'he00), .Enable(1'b1), .N(1'b0), .Z(1'b0), .C(1'b0), .V(1'b0), .Verified(Verified));  // open: Offset
  Conditionnal conditionnal_2 (
    .Instruction(16'he00), .Enable(1'b1), .N(1'b0), .Z(1'b0), .C(1'b1), .V(1'b1), .Verified(Verified_2));  // open: Offset
  Conditionnal conditionnal_3 (
    .Instruction(16'he00), .Enable(1'b1), .N(1'b1), .Z(1'b1), .C(1'b1), .V(1'b1), .Verified(Verified_3));  // open: Offset

  // Notes on the sheet:
  //   Any
endmodule

module Test_FlagAPSR1 (
  output [3:0] out_1
);

  wire clock_1_out;

  Clock clock_1 (.out(clock_1_out));
  FlagAPSR flagapsr_1 (.Flag_In(4'b0001), .Update_Mask(4'b0001), .Clk(clock_1_out), .Reset(1'b0), .Flag_Out(out_1));
endmodule

module Test_FlagAPSR2 (
  output [3:0] out_1
);

  wire clock_1_out;

  Clock clock_1 (.out(clock_1_out));
  FlagAPSR flagapsr_1 (.Flag_In(4'b0010), .Update_Mask(4'b0001), .Clk(clock_1_out), .Reset(1'b0), .Flag_Out(out_1));
endmodule

module Test_Program_Counter1 (
  output [7:0] out_1
);

  wire clock_1_out;

  Program_counter program_counter_1 (
    .Data(8'h2), .Count(1'b0), .UpDown(1'b1), .Load(1'b1), .Clk(clock_1_out), .Clear(1'b0), .Output(out_1));  // open: Carry
  Clock clock_1 (.out(clock_1_out));
endmodule

module Test_Program_Counter2 (
  output [7:0] out_1
);

  wire clock_1_out;

  Program_counter program_counter_1 (
    .Data({8{1'b0}}), .Count(1'b1), .UpDown(1'b1), .Load(1'b0), .Clk(clock_1_out), .Clear(1'b0),
    .Output(out_1));  // open: Carry
  Clock clock_1 (.out(clock_1_out));
endmodule

module Test_SP_Address1 (
  output [31:0] out_1
);

  SP_Address sp_address_1 (
    .Instruction(16'ha0), .Stack_Pointer(32'hfff), .Enable(1'b1), .New_Stack_Pointer(out_1));  // open: Write_Enable

  // Notes on the sheet:
  //   -010 0000
endmodule

module Test_SP_Address2 (
  output [31:0] out_1
);

  SP_Address sp_address_1 (
    .Instruction(16'h70), .Stack_Pointer({32{1'b0}}), .Enable(1'b1), .New_Stack_Pointer(out_1));  // open: Write_Enable

  // Notes on the sheet:
  //   +111 0000
endmodule
